# Fritzing sketch Sketch Sensores Unidos (saved by Fritzing 0.9.3b)

parts:
  Componente4 = Arduino Pro Mini v13
  Componente6 = Bluetooth HC-05 Macho
  microSD2 = MicroSD Card Module
  J1 = female pin header, 2 pins [form="♀ (female)"]
  J2 = female pin header, 2 pins [form="♀ (female)"]
  U1 = LIPO-1000mAh [package=lipo-1000]
  Componente8 = InvenSense MPU6050

nets:
  N1: Componente4.A4, Componente8.SDA, Componente8.XDA, Componente8.XCL
  N2: Componente4.A5, Componente8.SCL
  N3: Componente4.RAW, U1.+
  N4: Componente4.GND, J2.pin1, U1.-
  N5: Componente4.VCC, J1.pin2
  N6: Componente4.D13/SCK, microSD2.SCK
  N7: Componente4.D12/MISO, microSD2.MISO
  N8: Componente4.D11_PWM/MOSI, microSD2.MOSI
  N9: Componente4.D4, Componente4.D3_PWM, microSD2.CS
  N10: Componente4.D1/RX, Componente6.TXD
  N11: Componente4.D0/TX, Componente6.RXD
  VCC: Componente6.VCC, microSD2.VCC, J1.pin1, Componente8.VCC
  GND: Componente6.GND, microSD2.GND, J2.pin2, Componente8.GND

notes:
  El sensor usador es el Gy-86, sin embargo en fritzing el mas parecido es el MPU6050
  Vcc-------->
  3.3v*------>
  gnd*------>
  scl*------->
  sda*------>
  *que tienen conexion
  Son dos baterias de 3.7v y 1100 mAh
  SDA->A4
  SCL->A5
